# Fritzing sketch ProjetIOT (saved by Fritzing 0.9.4)
breadboards: 1

parts:
  Composant1 = Thumb Joystick
  Composant2 = Arduino Uno (Rev3)
  S1 = Pushbutton [package="[THT]"]
  S2 = Pushbutton [package="[THT]"]
  S3 = Pushbutton [package="[THT]"]
  S4 = Pushbutton [package="[THT]"]
  S5 = Pushbutton [package="[THT]"]
  S6 = Pushbutton [package="[THT]"]
  Grove1 = Grove Infrared Emitter

nets:
  GND: Composant1.GND, Composant2.GND, S1.Pin_3, S1.Pin_4, S2.Pin_3, S2.Pin_4, S3.Pin_1, S3.Pin_2, S4.Pin_1, S4.Pin_2, S5.Pin_3, S5.Pin_4, S6.Pin_3, S6.Pin_4, Grove1.GND
  N1: Composant1.SEL, Composant2.D10_PWM/SS
  N2: Composant1.HORZ, Composant2.A1
  N3: Composant1.VERT, Composant2.A0
  VCC: Composant1.VCC, Composant2.5V, Grove1.VCC
  N4: Composant2.D11_PWM/MOSI, Grove1.TX
  N5: Composant2.D2, S2.Pin_1, S2.Pin_2
  N6: Composant2.D3_PWM, S1.Pin_1, S1.Pin_2
  N7: Composant2.D4, S6.Pin_1, S6.Pin_2
  N8: Composant2.D5_PWM, S5.Pin_1, S5.Pin_2
  N9: Composant2.D6_PWM, S3.Pin_3, S3.Pin_4
  N10: Composant2.D7, S4.Pin_3, S4.Pin_4
